# Fritzing sketch esp-board (saved by Fritzing 0.9.3b)
breadboards: 1

parts:
  WeMos_D1_Mini1 = WeMos D1 Mini
  U1 = 74HC595 [package="DIP16 [THT]"]
  Tiny_RTC1 = Tiny RTC
  R1 = Resistor [tolerance=±5% resistance=4.7k package=THT]
  R2 = Resistor [tolerance=±5% resistance=4.7k package=THT]
  Factory_Reset_SW = SWITCH-MOMENTARY-2 [package=tactile_switch_tall]
  R3 = Resistor [tolerance=±5% resistance=4.7k package=THT]
  IC1 = ADS1115 16-bit ADC Breakout
  Analog_Sensor_Boards_(pH_EC) = Header 4 [package=screwterminal-3.5mm-4_lock]
  Digital_IO_(Relay_board_Transistors) = Header 6 [package=1x06-smd-female-v2]
  Digital_IO_(Relay_board_Transistors)_2 = Header 2 [package=molex-1x2_lock]
  R4 = Resistor [tolerance=±5% resistance=3.3k package=THT]
  R5 = Resistor [tolerance=±5% resistance=1k package=THT]
  R6 = Resistor [tolerance=±5% resistance=620 package=THT]
  R7 = Resistor [tolerance=±5% resistance=220 package=THT]
  R8 = Resistor [tolerance=±5% resistance=10k package=THT]
  C1 = Ceramic Capacitor [capacitance=100nF package="100 mil [THT, multilayer]"]
  S1 = SWITCH-MOMENTARY-2 [package=tactile-pth]
  S2 = SWITCH-MOMENTARY-2 [package=tactile-pth]
  S3 = SWITCH-MOMENTARY-2 [package=tactile-pth]
  S4 = SWITCH-MOMENTARY-2 [package=tactile-pth]
  S5 = SWITCH-MOMENTARY-2 [package=tactile-pth]
  Other_I2C_Stuff_(LCD_Arduino_Experimental_Boards) = Header 4 [package=screwterminal-3.5mm-4_lock]
  Future_Use/Optional = Header 2 [package=jst-2-pth-kit]

nets:
  3V3: WeMos_D1_Mini1.3V3, U1.MR, U1.VCC, R1.Pin_1, R2.Pin_1, R3.Pin_1, IC1.VDD, R8.Pin_0, Other_I2C_Stuff_(LCD_Arduino_Experimental_Boards).1
  5V: WeMos_D1_Mini1.5V, Tiny_RTC1.VCC
  N1: WeMos_D1_Mini1.A0, R7.Pin_0, R8.Pin_1, C1.0, S1.1
  N2: WeMos_D1_Mini1.D0, U1.SH_CP
  N3: WeMos_D1_Mini1.D1, Tiny_RTC1.SDA, R2.Pin_0, IC1.SDA, Other_I2C_Stuff_(LCD_Arduino_Experimental_Boards).4
  N4: WeMos_D1_Mini1.D2, Tiny_RTC1.SCL, R1.Pin_0, IC1.SCL, Other_I2C_Stuff_(LCD_Arduino_Experimental_Boards).3
  N5: WeMos_D1_Mini1.D3, Factory_Reset_SW.1
  DS18B20 Sensor board: WeMos_D1_Mini1.D5, R3.Pin_0
  N6: WeMos_D1_Mini1.D6, U1.DS
  AM2302 Sensor board: WeMos_D1_Mini1.D7
  N7: WeMos_D1_Mini1.D8, U1.ST_CP
  N8: WeMos_D1_Mini1.G, U1.GND, U1.OE, Factory_Reset_SW.2
  N9: U1.Q1, Digital_IO_(Relay_board_Transistors)_2.1
  N10: U1.Q2, Digital_IO_(Relay_board_Transistors).6
  N11: U1.Q3, Digital_IO_(Relay_board_Transistors).5
  N12: U1.Q4, Digital_IO_(Relay_board_Transistors).4
  N13: U1.Q5, Digital_IO_(Relay_board_Transistors).3
  N14: U1.Q6, Digital_IO_(Relay_board_Transistors).2
  N15: U1.Q7, Digital_IO_(Relay_board_Transistors).1
  N16: U1.Q0, Digital_IO_(Relay_board_Transistors)_2.2
  GND: Tiny_RTC1.GND, IC1.GND, Other_I2C_Stuff_(LCD_Arduino_Experimental_Boards).2
  N17: Tiny_RTC1.SQ, Future_Use/Optional.2
  N18: IC1.A0, Analog_Sensor_Boards_(pH_EC).4
  N19: IC1.A1, Analog_Sensor_Boards_(pH_EC).3
  N20: IC1.A2, Analog_Sensor_Boards_(pH_EC).2
  N21: IC1.A3, Analog_Sensor_Boards_(pH_EC).1
  N22: R4.Pin_0, R5.Pin_1, S4.1
  N23: R4.Pin_1, S5.1
  N24: R5.Pin_0, R6.Pin_1, S3.1
  N25: R6.Pin_0, R7.Pin_1, S2.1
  N26: C1.1, S1.2, S2.2, S3.2, S4.2, S5.2

custom parts:
  Tiny RTC: Tiny RTC I2C module DS1370Z RTC and AT24C32 EEPROM
  ADS1115 16-bit ADC Breakout: ADS1015 12-bit I2C ADC+PGA Breakout
